# Fritzing sketch scheme (saved by Fritzing 0.9.3b)
breadboards: 1

parts:
  U1 = NodeMCU V1.0
  IC1 = MCP23017 I2C I/O Expander
  U2 = 4-Channel 5v Relay Shield [package=relay-4ch5v10a]
  S1 = Pushbutton [package="[SMD]"]
  S2 = Pushbutton [package="[SMD]"]
  S3 = Pushbutton [package="[SMD]"]
  S4 = Pushbutton [package="[SMD]"]

nets:
  GND: U1.GND, U2.GND
  VIN: U1.Vin, U1.SD0, U2.VCC
  N1: IC1.GPB0, IC1.GPB1, IC1.GPB2, IC1.VDD, IC1.A1, IC1.A2, IC1.RESET, S1.Pin_1, S1.Pin_2, S1.Pin_3, S1.Pin_4, S2.Pin_1, S2.Pin_2, S2.Pin_3, S2.Pin_4, S3.Pin_1, S3.Pin_2, S3.Pin_3, S3.Pin_4, S4.Pin_1, S4.Pin_2, S4.Pin_3, S4.Pin_4
  N2: IC1.GPA1, U2.IN1
  N3: IC1.GPA2, U2.IN2
  N4: IC1.GPA3, U2.IN3
  N5: IC1.GPA4, U2.IN4

notes:
  to DHT22 module DAT

custom parts:
  NodeMCU V1.0: ESP8266 based NodeMCU
  MCP23017 I2C I/O Expander: The MCP23017 uses two i2c pins (these can be shared with other i2c devices), and in exchange gives you 16 general purpose pins. You can set each of 16 pins to be input, output, input with a pullup or open drain. There's even the ability to get an interrupt via an external pin when any of the inputs change so you don't have to keep polling the chip.
  4-Channel 5v Relay Shield: 4 Channel 5v Relay Shield w. 2x SPD-06VDC-SD-C
